// Digital circuit CPU.dig as structural Verilog
module CPU (
  input  Clock,
  input  Sel,
  input  Clock_2,
  input  ROM_EN,
  input  [17:0] ROM_DATA,
  input  [2:0] Physical_add,
  input  Clock_3,
  output [4:0] R_4_0,
  output [4:0] B,
  output [4:0] A,
  output [17:0] RAM_data,
  output [1:0] OP
);

  wire CF, Im_sel, JMP_SEL, Reg_EN, SF, ZF;
  wire [2:0] _3_bit_pc_adder_1_o_2_0, _3_bit_program_counter_1_o_2_0, multiplexer_1_out;
  wire [4:0] _5_bit_reg_with_4_reg_1_b_4_0;

  Multiplexer #(.Bits(3)) multiplexer_1 (
    .sel(JMP_SEL), .in_0(_3_bit_pc_adder_1_o_2_0), .in_1(RAM_data[13:11]), .out(multiplexer_1_out));
  _3_bit_program_counter _3_bit_program_counter_1 (
    .I_2_0(multiplexer_1_out), .Sel(Sel), .Clock(Clock), .O_2_0(_3_bit_program_counter_1_o_2_0));
  _3_bit_PC_adder _3_bit_pc_adder_1 (.I_2_0(_3_bit_program_counter_1_o_2_0), .O_2_0(_3_bit_pc_adder_1_o_2_0));
  _7_18_SRAM _7_18_sram_1 (
    .RA1_2_0(_3_bit_program_counter_1_o_2_0), .RA2_2_0(_3_bit_program_counter_1_o_2_0),
    .WA_2_0(Physical_add), .WD_17_0(ROM_DATA), .WE(ROM_EN), .Clock(Clock_2), .RD1_17_0(RAM_data));  // open: RD2_17_0
  _5_bit_reg_with_4_reg _5_bit_reg_with_4_reg_1 (
    .Rb_1_0(RAM_data[11:10]), .Ra_1_0(RAM_data[13:12]), .Wr_1_0(RAM_data[13:12]), .Clock(Clock_3),
    .WE(Reg_EN), .Wrd_4_0(R_4_0), .A_4_0(A), .B_4_0(_5_bit_reg_with_4_reg_1_b_4_0));
  Control_Unit control_unit_1 (
    .OP_3_0(RAM_data[17:14]), .ZF(ZF), .SF(SF), .OP_1_0(OP), .Im_sel(Im_sel), .Reg_EN(Reg_EN),
    .JMP_SEL(JMP_SEL));
  Multiplexer #(.Bits(5)) multiplexer_2 (
    .sel(Im_sel), .in_0(_5_bit_reg_with_4_reg_1_b_4_0), .in_1(RAM_data[11:7]), .out(B));
  _5_bit_ALU _5_bit_alu_1 (
    .B_4_0(B), .A_4_0(A), .OP_1_0(OP), .Carry_flag(CF), .R_4_0(R_4_0), .Sign_flag(SF), .Zero_flag(ZF));
endmodule
